# Fritzing sketch iBoard01 (saved by Fritzing 0.9.4)
breadboards: 1

parts:
  Part2 = Arduino Mega 2560 (Rev3)
  J36 = Basic Servo
  R4 = Resistor [tolerance=±5% resistance=220 package="2010 [SMD]"]
  R5 = Resistor [tolerance=±5% resistance=220 package="2010 [SMD]"]
  R6 = Resistor [tolerance=±5% resistance=220 package="2010 [SMD]"]
  S34 = SWITCH-MOMENTARY-2 [package=reed_switch_plastic]
  U2 = NodeMCU V3.0
  LED77 = RGB LED (com. cathode, rbg) [package="5 mm [THT]"]
  R7 = Resistor [tolerance=±5% resistance=1k package="2010 [SMD]"]

nets:
  GND: Part2.GND, J36.gnd, S34.2, U2.GND, LED77.common_cathode
  3V3: Part2.3V3, U2.Vin
  5V: Part2.5V, J36.vcc, R7.Pin_0
  N1: Part2.D0_RX0, U2.TX
  N2: Part2.D1_TX0, U2.RX
  N3: Part2.D2_PWM, S34.1, R7.Pin_1
  N4: Part2.D3_PWM, R6.Pin_0
  N5: Part2.D4_PWM, R5.Pin_0
  N6: Part2.D5_PWM, R4.Pin_0
  N7: Part2.D6_PWM, J36.pulse
  N8: R4.Pin_1, LED77.red_anode
  N9: R5.Pin_1, LED77.blue_anode
  N10: R6.Pin_1, LED77.green_anode

custom parts:
  NodeMCU V3.0: ESP8266 based NodeMCU
